# Fritzing sketch web-weather (saved by Fritzing 0.7.5b)
breadboards: 1

parts:
  Arduino1 = Arduino  # not connected
  Arduino_Ethernet_Shield1 = Arduino Ethernet Shield
  Componente2 = Real Time Clock Module - DS1307 RTC Breakout Board
  Componente3 = Humidity Temperature Sensor SHT15

nets:
  N1: Arduino_Ethernet_Shield1.D7, Componente3.SDA
  GND: Arduino_Ethernet_Shield1.GND, Componente3.GND
  N2: Arduino_Ethernet_Shield1.A4, Componente2.SDA
  N3: Arduino_Ethernet_Shield1.A5, Componente2.SCL
  5V: Componente2.5V, Componente3.VCC

notes:
  Insert an SD Card into the slot on the Ethernet Shield.
